# Fritzing sketch L298N_baglanti_sol_motor_baglanti (saved by Fritzing 1.0.2b)
breadboards: 1

parts:
  L298N1 = L298N DC motor driver
  M2 = DC Motor [voltage_(max)=6V voltage_(min)=3V]
  U1 = LIPO-2000mAh [package=lipo-2000]
  T3_Vakfı1 = Generic shrouded header - 32 pins [package=THT]

nets:
  N1: L298N1.OUT1, M2.pin_2
  N2: L298N1.OUT2, M2.pin_1
  N3: L298N1.12V, U1.+
  N4: L298N1.GND, U1.-, T3_Vakfı1.pin32
  N5: L298N1.5V, L298N1.ENA
  N6: L298N1.IN1, T3_Vakfı1.pin12
  N7: L298N1.IN2, T3_Vakfı1.pin11

notes:
  2 x 3.7 V LiPo Batteries connected in series
  Left Motor
  L298N Motor Driver Board

custom parts:
  L298N DC motor driver: 2x DC motor driver with 78M05 positive voltage regulator (7..35 V) L298N: max 46 V, 2 A Set 5 V Enable jumper to enable 5 V regultor (needed for the L298N) and +5 V output at screw terminal or supply external +5 V at screw terminal Set ENA and/or ENB to +5 V to enable motor permanently or supply ENA and/or ENB with PWM signal IN1 and IN2 set rotation directory for motor A (OUT1/OUT2) IN2 and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
  Generic shrouded header - 32 pins: Ülkemizin mühendislik kaynakları kullanılarak geliştirilen Deneyap Kart; güçlü işlemcisi, dayanıklı tasarımı ve çok yönlü giriş/çıkış pinleri ile kullanıcılara Elektronik Programlama, Nesnelerin İnterneti (IoT) ve Yapay Zeka alanlarında başlangıç seviyesinden endüstriyel uygulamalara kadar her seviyede projeyi yapma imkanı sunuyor.
